// Digital circuit Somador4Bit.dig as structural Verilog
module Somador4Bit (
  input  A1,
  input  B1,
  input  C0,
  input  A2,
  input  B2,
  input  A3,
  input  B3,
  input  A4,
  input  B4,
  output S1,
  output S2,
  output S3,
  output S4,
  output C4
);

  wire somador1bit_1_cout, somador1bit_2_cout, somador1bit_3_cout;

  Somador1Bit somador1bit_1 (.Cin(C0), .A(A1), .B(B1), .S(S1), .Cout(somador1bit_1_cout));
  Somador1Bit somador1bit_2 (.Cin(somador1bit_1_cout), .A(A2), .B(B2), .S(S2), .Cout(somador1bit_2_cout));
  Somador1Bit somador1bit_3 (.Cin(somador1bit_2_cout), .A(A3), .B(B3), .S(S3), .Cout(somador1bit_3_cout));
  Somador1Bit somador1bit_4 (.Cin(somador1bit_3_cout), .A(A4), .B(B4), .S(S4), .Cout(C4));
  Seven_Seg_Hex seven_seg_hex_1 (.d({S4, S3, S2, S1}), .dp(1'b0));
endmodule
